# Fritzing sketch diagram (saved by Fritzing 0.9.6b)
breadboards: 1

parts:
  Part1 = Arduino Nano (Rev3.0)
  R1 = Resistor [tolerance=±5% power=0.25 resistance=10k package=THT]
  R2 = PHOTOCELL [package=photocell]
  J1 = Basic Servo
  VCC1 = Battery block 9V

nets:
  N1: Part1.D3, J1.pulse
  N2: Part1.A0, R1.Pin_1, R2.P$1
  N3: R1.Pin_0, J1.vcc, VCC1.+
  N4: R2.P$2, J1.gnd, VCC1.-
